// Logisim project electronic quiz buzzer circuit.circ as structural Verilog: 1 circuit, main circuit main
module main (
  input  x2,
  input  x1,
  input  x0,
  input  clr,
  output S1,
  output S0,
  output BUZZER
);

  wire and_1_out, and_2_out, and_3_out, and_4_out, and_5_out, and_6_out, and_7_out, and_8_out, and_9_out,
       and_10_out, and_11_out, and_12_out, and_13_out, clock_1_out, d_ff_1_qn, d_ff_2_qn, not_1_out,
       not_2_out, not_3_out, not_4_out, not_5_out, not_6_out, not_7_out, not_8_out, not_9_out, not_10_out,
       not_11_out, or_1_out, or_2_out, or_3_out, or_4_out;

  and and_1 (and_1_out, x1, not_4_out);
  or or_1 (or_1_out, and_1_out, and_2_out);
  and and_2 (and_2_out, x2, not_5_out);
  not not_1 (not_1_out, S0);
  not not_2 (not_2_out, S1);
  and and_3 (and_3_out, S1, not_3_out, S0);
  not not_3 (not_3_out, clr);
  and and_4 (and_4_out, S1, not_3_out, not_1_out);
  and and_5 (and_5_out, not_3_out, not_1_out, not_2_out, or_1_out, not_6_out);
  not not_4 (not_4_out, x2);
  Clock clock_1 (.out(clock_1_out));
  or or_2 (or_2_out, and_3_out, and_4_out, and_5_out);
  not not_5 (not_5_out, x1);
  D_Flip_Flop d_ff_1 (.clk(clock_1_out), .D(or_2_out), .Q(S1), .Qn(d_ff_1_qn), .reset(clr));  // open: preset, en
  not not_6 (not_6_out, x0);
  D_Flip_Flop d_ff_2 (.clk(clock_1_out), .D(or_4_out), .Q(S0), .Qn(d_ff_2_qn), .reset(clr));  // open: preset, en
  and and_6 (and_6_out, not_6_out, x2);
  and and_7 (and_7_out, S1, S0);
  and and_8 (and_8_out, d_ff_1_qn, d_ff_2_qn, not_5_out);
  not not_7 (not_7_out, clr);
  or or_3 (or_3_out, and_6_out, and_9_out);
  and and_9 (and_9_out, not_4_out, x0);
  and and_10 (and_10_out, S1, not_9_out);
  or or_4 (or_4_out, and_11_out, and_3_out, and_12_out);
  and and_11 (and_11_out, and_8_out, not_7_out, or_3_out);
  not not_8 (not_8_out, S1);
  not not_9 (not_9_out, S0);
  and and_12 (and_12_out, S0, not_10_out, not_11_out);
  and and_13 (and_13_out, not_8_out, S0);
  not not_10 (not_10_out, clr);
  not not_11 (not_11_out, S1);
  LED led_1 (.in(and_7_out));
  or or_5 (BUZZER, and_7_out, and_7_out, and_13_out);
  LED led_2 (.in(and_10_out));
  LED led_3 (.in(and_13_out));

  // Notes on the sheet:
  //   Q1 Q0
  //   Q1 Q'0
  //   Q'1 Q'0 X'0
  //   D1
  //   D0
  //   Z2
  //   Z1
  //   Z0
endmodule
